# Fritzing sketch GarageRemote2 (saved by Fritzing 0.9.4)
stripboards: 1

parts:
  U1 = attiny85 [package=dip]
  C1 = Ceramic Capacitor [capacitance=100nF package="100 mil [THT, multilayer]"]
  R3 = Resistor [tolerance=±5% resistance=4.7k package=THT]
  LED1 = LED - 5mm [color="Red (633nm)" package="5 mm [THT]"]
  C3 = Ceramic Capacitor [capacitance=100nF package="100 mil [THT, multilayer]"]
  S1 = Pushbutton [package="[THT]"]
  C4 = Ceramic Capacitor [capacitance=330nF voltage=16V package="100 mil [THT, multilayer]"]
  D1 = Rectifier Diode [part_number=1N5817 package="300 mil [THT]"]
  R4 = Resistor [tolerance=±5% resistance=2k package=THT]
  IC3 = Voltage Regulator [package=to-92]
  U3 = H34A [package=THT]
  J1 = female pin header, 2 pins [form="♀ (female)"]
  J2 = female pin header, 2 pins [form="♀ (female)"]
  BAT2 = Battery Holders [package=battery-aaa]

nets:
  N1: U1.Pin_1, C1.1, R3.Pin_1
  GND: U1.Pin_4, C1.0, LED1.cathode, C3.0, C4.1, IC3.GND, U3.GND, J2.pin2, BAT2.-
  N2: U1.Pin_5, R4.Pin_1, U3.DAT
  N3: U1.Pin_6, J1.pin1
  N4: U1.Pin_7, J1.pin2
  N5: U1.Pin_8, R3.Pin_0, C3.1, IC3.OUT
  N6: LED1.anode, R4.Pin_0
  N7: S1.Pin_2, D1.cathode
  N8: S1.Pin_3, S1.Pin_4, C4.0, IC3.IN, U3.Vcc
  N9: D1.anode, BAT2.+

custom parts:
  Voltage Regulator: Voltage Regulator 78L05 5V 100mA regulator. IGO (Input Ground Output).
  H34A: H34A 433Mhz Mini Wireless Transmitter Module ASK 2.6-12V (Dat Vcc GND Ant)
